# Fritzing sketch sodochan (saved by Fritzing 0.9.3b)

parts:
  U1 = ESP32-38PinWide [part_number=ESP32-38PinWide]
  DHT1 = Humidity and Temperature Sensor DHT11
  PART1 = SparkFun Soil Moisture Sensor [part_number=SEN-13322]
  S1 = Round Pushbutton
  S2 = Round Pushbutton
  KY-1 = Keyes Relay [package=THT]
  S3 = Round Pushbutton  # not connected
  KY-2 = Keyes Relay [package=THT]

nets:
  VCC: U1.3.3, DHT1.Vcc, PART1.VCC, S1.leg0, S2.leg0, KY-1.power, KY-2.power
  N1: U1.GPIO34, PART1.SIG
  N2: U1.GPIO14, S2.leg1
  N3: U1.GPIO11, PART1.GND
  N4: U1.GPIO15, S1.leg1
  N5: U1.GPIO4, DHT1.Data-signal
  N6: U1.GPIO18, KY-2.signal
  N7: U1.GPIO19, KY-1.signal
  N8: U1.GND, DHT1.GND_1, KY-1.ground, KY-2.ground

custom parts:
  ESP32-38PinWide: Generic 38-Pin ESP32 with wide format (only access to one side of pins on a breadboard) based on Stephen Lilley's HiLetgo ESP-WROOM-32 ESP32 ESP-32S Development Board.
  Humidity and Temperature Sensor DHT11: Digital relative humidity & temperature sensor DHT11
  SparkFun Soil Moisture Sensor: The SparkFun Soil Moisture Sensor is a simple breakout for measuring the moisture in soil and similar materials.
  Keyes Relay: The Keyes 5V relay module is suitable for SCM development, home appliance control. It uses a 5V~12V TIL control signal which can control DC / AC signal.
